// Logisim project Processor_Last edited.circ as structural Verilog: 6 circuits, main circuit main
module main (
  output out_1
);

  wire alu_control_unit_1_bin, clock_1_out, control_unit_1_alu_src, control_unit_1_branch_and_equal,
       control_unit_1_branch_and_not_equal, control_unit_1_jump, control_unit_1_reg_to_dest,
       control_unit_1_reg_write, or_1_out;
  wire [1:0] alu_control_unit_1_s1__s0, control_unit_1_alu_op;
  wire [4:0] multiplexer_1_out;
  wire [5:0] rom_1_data_2;
  wire [15:0] bit_extender_1_out;
  wire [31:0] adder_1_out, adder_2_out, alu_1_out_6, bit_extender_2_out, multiplexer_2_out,
       multiplexer_3_out, multiplexer_4_out, n32_register_1_rs_output, n32_register_1_rt_output, register_1_q;
  wire [31:6] rom_1_data;

  Clock clock_1 (.out(clock_1_out));
  Register #(.width(32)) register_1 (.D(multiplexer_4_out), .Q(register_1_q), .clk(clock_1_out));  // open: en, clr
  Adder #(.width(32)) adder_1 (.a(32'h1), .b(register_1_q), .out(adder_1_out));  // open: cin, cout
  Bit_Extender #(.in_width(32)) bit_extender_1 (.in(register_1_q), .out(bit_extender_1_out));
  ROM #(.addrWidth(16), .dataWidth(32)) rom_1 (
    .addr(bit_extender_1_out), .data({rom_1_data, rom_1_data_2}));  // open: sel
  Multiplexer #(.width(5), .enable("false")) multiplexer_1 (
    .in0(rom_1_data[20:16]), .in1(rom_1_data[15:11]), .out(multiplexer_1_out),
    .sel(control_unit_1_reg_to_dest));
  assign bit_extender_2_out = {{16{1'b0}}, {rom_1_data[15:6], rom_1_data_2}};  // Bit_Extender bit_extender_2
  Control_Unit control_unit_1 (
    .in_1(rom_1_data[31:26]), .Reg_To_Dest(control_unit_1_reg_to_dest), .ALU_src(control_unit_1_alu_src),
    .Reg_write(control_unit_1_reg_write), .Branch_and_equal(control_unit_1_branch_and_equal),
    .Branch_and_not_equal(control_unit_1_branch_and_not_equal), .Jump(control_unit_1_jump),
    .ALu_op(control_unit_1_alu_op));  // open: Mem_to_Read
  _32_Register u_32_register_1 (
    .Data_Write(alu_1_out_6), .RS_Output(n32_register_1_rs_output), .RT_Output(n32_register_1_rt_output),
    .RegWrite(control_unit_1_reg_write), .RD(multiplexer_1_out), .RT(rom_1_data[20:16]),
    .RS(rom_1_data[25:21]), .Clock(clock_1_out));
  Multiplexer #(.width(32), .enable("false")) multiplexer_2 (
    .in0(n32_register_1_rt_output), .in1(bit_extender_2_out), .out(multiplexer_2_out),
    .sel(control_unit_1_alu_src));
  ALU_Control_Unit alu_control_unit_1 (
    .Function(rom_1_data_2), .ALU_OP(control_unit_1_alu_op), .S1__S0(alu_control_unit_1_s1__s0),
    .Bin(alu_control_unit_1_bin));
  ALU alu_1 (
    .RT_Value(multiplexer_2_out), .RS_Value(n32_register_1_rs_output), .out_6(alu_1_out_6),
    .ALU_Opp(alu_control_unit_1_s1__s0), .in_1(alu_control_unit_1_bin), .out_7(out_1),
    .Bin(alu_control_unit_1_bin));
  Adder #(.width(32)) adder_2 (.a(adder_1_out), .b(bit_extender_2_out), .out(adder_2_out));  // open: cin, cout
  or or_1 (or_1_out, control_unit_1_branch_and_equal, control_unit_1_branch_and_not_equal);
  Multiplexer #(.width(32)) multiplexer_3 (
    .in0(adder_1_out), .in1(adder_2_out), .out(multiplexer_3_out), .sel(or_1_out));  // open: en
  Multiplexer #(.width(32)) multiplexer_4 (
    .in0(multiplexer_3_out), .in1({adder_1_out[31:26], rom_1_data[25:6], rom_1_data_2}),
    .out(multiplexer_4_out), .sel(control_unit_1_jump));  // open: en

  // Notes on the sheet:
  //   contents of rom_1 (hex, n*v repeats v):
  //   11001 12001 13001 14001
endmodule

module ALU (
  input  in_1,
  input  [31:0] RT_Value,
  input  [31:0] RS_Value,
  input  Bin,
  input  [1:0] ALU_Opp,
  output [31:0] out_6,
  output out_7
);

  wire [31:0] adder_1_out, and_1_out, multiplexer_1_out, not_1_out, or_1_out;

  assign not_1_out = ~RT_Value;  // NOT_Gate not_1, 32 bits wide
  Adder #(.width(32)) adder_1 (.a(RS_Value), .b(multiplexer_1_out), .out(adder_1_out), .cin(in_1), .cout(out_7));
  Multiplexer #(.width(32), .enable("false")) multiplexer_1 (
    .in0(RT_Value), .in1(not_1_out), .out(multiplexer_1_out), .sel(Bin));
  assign and_1_out = RS_Value & RT_Value;  // AND_Gate and_1, 32 bits wide
  assign or_1_out = RS_Value | RT_Value;  // OR_Gate or_1, 32 bits wide
  Multiplexer #(.select(2), .width(32), .enable("false")) multiplexer_2 (
    .in0(adder_1_out), .in1(and_1_out), .in2(or_1_out), .out(out_6), .sel(ALU_Opp));  // open: in3
endmodule

module Control_Unit (
  input  [5:0] in_1,
  output Reg_To_Dest,
  output ALU_src,
  output Reg_write,
  output Mem_to_Read,
  output Branch_and_equal,
  output Branch_and_not_equal,
  output Jump,
  output [1:0] ALu_op
);

  wire Ori_out;

  and R_Type (Reg_To_Dest, ~in_1[5], ~in_1[4], ~in_1[3], ~in_1[2], ~in_1[1], ~in_1[0]);  // AND_Gate
  and Ori (Ori_out, ~in_1[5], ~in_1[4], ~in_1[3], ~in_1[2], ~in_1[1], in_1[0]);  // AND_Gate
  and LW (Mem_to_Read, ~in_1[5], ~in_1[4], ~in_1[3], ~in_1[2], in_1[1], ~in_1[0]);  // AND_Gate
  and BEQ (Branch_and_equal, ~in_1[5], ~in_1[4], ~in_1[3], ~in_1[2], in_1[1], in_1[0]);  // AND_Gate
  and BNE (Branch_and_not_equal, ~in_1[5], ~in_1[4], ~in_1[3], in_1[2], ~in_1[1], ~in_1[0]);  // AND_Gate
  and J (Jump, ~in_1[5], ~in_1[4], ~in_1[3], in_1[2], ~in_1[1], in_1[0]);  // AND_Gate
  or or_1 (ALu_op[0], Branch_and_equal, Ori_out, Branch_and_not_equal);
  or or_2 (ALu_op[1], Reg_To_Dest, Ori_out);
  or or_3 (ALU_src, Ori_out, Mem_to_Read);
  or or_4 (Reg_write, Reg_To_Dest, Ori_out, Mem_to_Read);
endmodule

module _32_Register (
  input  Clock,
  input  RegWrite,
  input  [31:0] Data_Write,
  input  [4:0] RS,
  input  [4:0] RD,
  input  [4:0] RT,
  output [31:0] RS_Output,
  output [31:0] RT_Output
);

  wire and_1_out, and_2_out, and_3_out, and_4_out, and_5_out, and_6_out, and_7_out, and_8_out, and_9_out,
       and_10_out, and_11_out, and_12_out, and_13_out, and_14_out, and_15_out, and_16_out, and_17_out,
       and_18_out, and_19_out, and_20_out, and_21_out, and_22_out, and_23_out, and_24_out, and_25_out,
       and_26_out, and_27_out, and_28_out, and_29_out, and_30_out, and_31_out, and_32_out, decoder_1_out0,
       decoder_1_out1, decoder_1_out2, decoder_1_out3, decoder_1_out4, decoder_1_out5, decoder_1_out6,
       decoder_1_out7, decoder_1_out8, decoder_1_out9, decoder_1_out10, decoder_1_out11, decoder_1_out12,
       decoder_1_out13, decoder_1_out14, decoder_1_out15, decoder_1_out16, decoder_1_out17, decoder_1_out18,
       decoder_1_out19, decoder_1_out20, decoder_1_out21, decoder_1_out22, decoder_1_out23, decoder_1_out24,
       decoder_1_out25, decoder_1_out26, decoder_1_out27, decoder_1_out28, decoder_1_out29, decoder_1_out30,
       decoder_1_out31;
  wire [31:0] register_1_q, register_2_q, register_3_q, register_4_q, register_5_q, register_6_q,
       register_7_q, register_8_q, register_9_q, register_10_q, register_11_q, register_12_q, register_13_q,
       register_14_q, register_15_q, register_16_q, register_17_q, register_18_q, register_19_q,
       register_20_q, register_21_q, register_22_q, register_23_q, register_24_q, register_25_q,
       register_26_q, register_27_q, register_28_q, register_29_q, register_30_q, register_31_q,
       register_32_q;

  Decoder #(.select(5), .enable("false")) decoder_1 (
    .out0(decoder_1_out0), .out1(decoder_1_out1), .out2(decoder_1_out2), .out3(decoder_1_out3),
    .out4(decoder_1_out4), .out5(decoder_1_out5), .out6(decoder_1_out6), .out7(decoder_1_out7),
    .out8(decoder_1_out8), .out9(decoder_1_out9), .out10(decoder_1_out10), .out11(decoder_1_out11),
    .out12(decoder_1_out12), .out13(decoder_1_out13), .out14(decoder_1_out14), .out15(decoder_1_out15),
    .out16(decoder_1_out16), .out17(decoder_1_out17), .out18(decoder_1_out18), .out19(decoder_1_out19),
    .out20(decoder_1_out20), .out21(decoder_1_out21), .out22(decoder_1_out22), .out23(decoder_1_out23),
    .out24(decoder_1_out24), .out25(decoder_1_out25), .out26(decoder_1_out26), .out27(decoder_1_out27),
    .out28(decoder_1_out28), .out29(decoder_1_out29), .out30(decoder_1_out30), .out31(decoder_1_out31),
    .sel(RD));
  and and_1 (and_1_out, RegWrite, decoder_1_out0);
  and and_2 (and_2_out, RegWrite, decoder_1_out1);
  and and_3 (and_3_out, RegWrite, decoder_1_out2);
  and and_4 (and_4_out, RegWrite, decoder_1_out3);
  and and_5 (and_5_out, RegWrite, decoder_1_out4);
  and and_6 (and_6_out, RegWrite, decoder_1_out5);
  and and_7 (and_7_out, RegWrite, decoder_1_out6);
  and and_8 (and_8_out, RegWrite, decoder_1_out7);
  and and_9 (and_9_out, RegWrite, decoder_1_out8);
  and and_10 (and_10_out, RegWrite, decoder_1_out9);
  and and_11 (and_11_out, RegWrite, decoder_1_out10);
  and and_12 (and_12_out, RegWrite, decoder_1_out11);
  and and_13 (and_13_out, RegWrite, decoder_1_out12);
  and and_14 (and_14_out, RegWrite, decoder_1_out13);
  and and_15 (and_15_out, RegWrite, decoder_1_out14);
  and and_16 (and_16_out, RegWrite, decoder_1_out15);
  and and_17 (and_17_out, RegWrite, decoder_1_out16);
  and and_18 (and_18_out, RegWrite, decoder_1_out17);
  and and_19 (and_19_out, RegWrite, decoder_1_out18);
  and and_20 (and_20_out, RegWrite, decoder_1_out19);
  and and_21 (and_21_out, RegWrite, decoder_1_out20);
  and and_22 (and_22_out, RegWrite, decoder_1_out21);
  and and_23 (and_23_out, RegWrite, decoder_1_out22);
  and and_24 (and_24_out, RegWrite, decoder_1_out23);
  and and_25 (and_25_out, RegWrite, decoder_1_out24);
  and and_26 (and_26_out, RegWrite, decoder_1_out25);
  and and_27 (and_27_out, RegWrite, decoder_1_out26);
  and and_28 (and_28_out, RegWrite, decoder_1_out27);
  and and_29 (and_29_out, RegWrite, decoder_1_out28);
  and and_30 (and_30_out, RegWrite, decoder_1_out29);
  and and_31 (and_31_out, RegWrite, decoder_1_out30);
  and and_32 (and_32_out, RegWrite, decoder_1_out31);
  Register #(.width(32)) register_1 (.D(Data_Write), .en(and_1_out), .Q(register_1_q), .clk(Clock));  // open: clr
  Register #(.width(32)) register_2 (.D(Data_Write), .en(and_2_out), .Q(register_2_q), .clk(Clock));  // open: clr
  Register #(.width(32)) register_3 (.en(and_3_out), .Q(register_3_q), .clk(Clock));  // open: D, clr
  Register #(.width(32)) register_4 (.D(Data_Write), .en(and_4_out), .Q(register_4_q), .clk(Clock));  // open: clr
  Register #(.width(32)) register_5 (.D(Data_Write), .en(and_5_out), .Q(register_5_q), .clk(Clock));  // open: clr
  Register #(.width(32)) register_6 (.D(Data_Write), .en(and_6_out), .Q(register_6_q), .clk(Clock));  // open: clr
  Register #(.width(32)) register_7 (.D(Data_Write), .en(and_7_out), .Q(register_7_q), .clk(Clock));  // open: clr
  Register #(.width(32)) register_8 (.D(Data_Write), .en(and_8_out), .Q(register_8_q), .clk(Clock));  // open: clr
  Register #(.width(32)) register_9 (.D(Data_Write), .en(and_9_out), .Q(register_9_q), .clk(Clock));  // open: clr
  Register #(.width(32)) register_10 (.D(Data_Write), .en(and_10_out), .Q(register_10_q), .clk(Clock));  // open: clr
  Register #(.width(32)) register_11 (.D(Data_Write), .en(and_11_out), .Q(register_11_q), .clk(Clock));  // open: clr
  Register #(.width(32)) register_12 (.D(Data_Write), .en(and_12_out), .Q(register_12_q), .clk(Clock));  // open: clr
  Register #(.width(32)) register_13 (.D(Data_Write), .en(and_13_out), .Q(register_13_q), .clk(Clock));  // open: clr
  Register #(.width(32)) register_14 (.D(Data_Write), .en(and_14_out), .Q(register_14_q), .clk(Clock));  // open: clr
  Register #(.width(32)) register_15 (.D(Data_Write), .en(and_15_out), .Q(register_15_q), .clk(Clock));  // open: clr
  Register #(.width(32)) register_16 (.D(Data_Write), .en(and_16_out), .Q(register_16_q), .clk(Clock));  // open: clr
  Register #(.width(32)) register_17 (.D(Data_Write), .en(and_17_out), .Q(register_17_q), .clk(Clock));  // open: clr
  Register #(.width(32)) register_18 (.D(Data_Write), .en(and_18_out), .Q(register_18_q), .clk(Clock));  // open: clr
  Register #(.width(32)) register_19 (.D(Data_Write), .en(and_19_out), .Q(register_19_q), .clk(Clock));  // open: clr
  Register #(.width(32)) register_20 (.D(Data_Write), .en(and_20_out), .Q(register_20_q), .clk(Clock));  // open: clr
  Register #(.width(32)) register_21 (.D(Data_Write), .en(and_21_out), .Q(register_21_q), .clk(Clock));  // open: clr
  Register #(.width(32)) register_22 (.D(Data_Write), .en(and_22_out), .Q(register_22_q), .clk(Clock));  // open: clr
  Register #(.width(32)) register_23 (.D(Data_Write), .en(and_23_out), .Q(register_23_q), .clk(Clock));  // open: clr
  Register #(.width(32)) register_24 (.D(Data_Write), .en(and_24_out), .Q(register_24_q), .clk(Clock));  // open: clr
  Register #(.width(32)) register_25 (.D(Data_Write), .en(and_25_out), .Q(register_25_q), .clk(Clock));  // open: clr
  Register #(.width(32)) register_26 (.D(Data_Write), .en(and_26_out), .Q(register_26_q), .clk(Clock));  // open: clr
  Register #(.width(32)) register_27 (.D(Data_Write), .en(and_27_out), .Q(register_27_q), .clk(Clock));  // open: clr
  Register #(.width(32)) register_28 (.D(Data_Write), .en(and_28_out), .Q(register_28_q), .clk(Clock));  // open: clr
  Register #(.width(32)) register_29 (.D(Data_Write), .en(and_29_out), .Q(register_29_q), .clk(Clock));  // open: clr
  Register #(.width(32)) register_30 (.D(Data_Write), .en(and_30_out), .Q(register_30_q), .clk(Clock));  // open: clr
  Register #(.width(32)) register_31 (.D(Data_Write), .en(and_31_out), .Q(register_31_q), .clk(Clock));  // open: clr
  Register #(.width(32)) register_32 (.D(Data_Write), .en(and_32_out), .Q(register_32_q), .clk(Clock));  // open: clr
  Multiplexer #(.select(5), .width(32)) multiplexer_1 (
    .in0(register_1_q), .in1(register_2_q), .in2(register_3_q), .in3(register_4_q), .in4(register_5_q),
    .in5(register_6_q), .in6(register_7_q), .in7(register_8_q), .in8(register_9_q), .in9(register_10_q),
    .in10(register_11_q), .in11(register_12_q), .in12(register_13_q), .in13(register_14_q),
    .in14(register_15_q), .in15(register_16_q), .in16(register_17_q), .in17(register_18_q),
    .in18(register_19_q), .in19(register_20_q), .in20(register_21_q), .in21(register_22_q),
    .in22(register_23_q), .in23(register_24_q), .in24(register_25_q), .in25(register_26_q),
    .in26(register_27_q), .in27(register_28_q), .in28(register_29_q), .in29(register_30_q),
    .in30(register_31_q), .in31(register_32_q), .out(RS_Output), .sel(RS));  // open: en
  Multiplexer #(.select(5), .width(32)) multiplexer_2 (
    .in0(register_1_q), .in1(register_2_q), .in2(register_3_q), .in3(register_4_q), .in4(register_5_q),
    .in5(register_6_q), .in6(register_7_q), .in7(register_8_q), .in8(register_9_q), .in9(register_10_q),
    .in10(register_11_q), .in11(register_12_q), .in12(register_13_q), .in13(register_14_q),
    .in14(register_15_q), .in15(register_16_q), .in16(register_17_q), .in17(register_18_q),
    .in18(register_19_q), .in19(register_20_q), .in20(register_21_q), .in21(register_22_q),
    .in22(register_23_q), .in23(register_24_q), .in24(register_25_q), .in25(register_26_q),
    .in26(register_27_q), .in27(register_28_q), .in28(register_29_q), .in29(register_30_q),
    .in30(register_31_q), .in31(register_32_q), .out(RT_Output), .sel(RT));  // open: en

  // Notes on the sheet:
  //   Ridwanul Haque
  //   1721144042
endmodule

module Functon_unit (
  input  [5:0] Function_unit,
  input  [1:0] Alu_op,
  output [1:0] oparation
);

  wire and_2_out, and_3_out, not_1_out, not_2_out, not_3_out;

  not not_1 (not_1_out, Alu_op[1]);
  not not_2 (not_2_out, Function_unit[1]);
  not not_3 (not_3_out, Function_unit[0]);
  and and_1 (oparation[0], Function_unit[0], Alu_op[1]);
  and and_2 (and_2_out, not_2_out, Function_unit[2]);
  and and_3 (and_3_out, Function_unit[1], not_3_out, Function_unit[2]);
  or or_1 (oparation[1], and_2_out, and_3_out, not_1_out);
endmodule

module ALU_Control_Unit (
  input  [5:0] Function,
  input  [1:0] ALU_OP,
  output [1:0] S1__S0,
  output Bin
);

  wire not_1_out, not_2_out;

  not not_1 (not_1_out, ALU_OP[0]);
  and and_1 (S1__S0[0], Function[0], Function[1]);
  and and_2 (S1__S0[1], ALU_OP[0], not_2_out);
  not not_2 (not_2_out, Function[0]);
  and and_3 (Bin, not_1_out, ALU_OP[1]);
endmodule
